# Fritzing sketch WR-mon-cafe_rifin (saved by Fritzing 0.9.10b)
circuit board: 12cm x 8cm
breadboards: 2

parts:
  Esp32_GND->3_3V = female pin header, 17 pins [form="♀ (female)"]
  VS1053_5V->XDCS = female pin header, 9 pins [form="♀ (female)"]
  ESP32_3_3V->GND = female pin header, 17 pins [form="♀ (female)"]
  IR = female pin header, 3 pins [form="♀ (female)"]
  74HC14 = Hex Inverter Schmitt Trigger SN74HC14 [package="DIP (Dual Inline)"]
  C1 = Electrolytic Capacitor [capacitance=1000μF voltage=35V package="1010 [SMD, electrolytic]"]
  ST7789_BL->GND = female pin header, 8 pins [form="♀ (female)"]
  Rele = female pin header, 3 pins [form="♀ (female)"]
  R1 = Resistor [tolerance=±5% power=0.25W resistance=10k package=THT]
  R2 = Resistor [tolerance=±5% power=0.25W resistance=10k package=THT]
  C2 = Electrolytic Capacitor [capacitance=0.1µF voltage=50V package="100 mil [THT, electrolytic]"]
  ON = female pin header, 2 pins [form="♀ (female)"]
  R3 = Resistor [tolerance=±5% power=0.25W resistance=10k package=THT]
  VUp = female pin header, 2 pins [form="♀ (female)"]
  R4 = Resistor [tolerance=±5% power=0.25W resistance=10k package=THT]
  C3 = Electrolytic Capacitor [capacitance=0.1µF voltage=50V package="100 mil [THT, electrolytic]"]
  R5 = Resistor [tolerance=±5% power=0.25W resistance=10k package=THT]
  R6 = Resistor [tolerance=±5% power=0.25W resistance=10k package=THT]
  VDn = female pin header, 2 pins [form="♀ (female)"]
  C4 = Electrolytic Capacitor [capacitance=100nF voltage=50V package="100 mil [THT, electrolytic]"]
  R7 = Resistor [tolerance=±5% power=0.25W resistance=10k package=THT]
  C5 = Electrolytic Capacitor [capacitance=0.1µF voltage=50V package="100 mil [THT, electrolytic]"]
  C6 = Electrolytic Capacitor [capacitance=0.1µF voltage=50V package="100 mil [THT, electrolytic]"]
  R8 = Resistor [tolerance=±5% power=0.25W resistance=10k package=THT]
  R9 = Resistor [tolerance=±5% power=0.25W resistance=10k package=THT]
  R10 = Resistor [tolerance=±5% power=0.25W resistance=10k package=THT]
  ChUp = female pin header, 2 pins [form="♀ (female)"]
  ChDn = female pin header, 2 pins [form="♀ (female)"]
  Power_5V = female pin header, 2 pins [form="♀ (female)"]

nets:
  N1: Esp32_GND->3_3V.pin2, VS1053_5V->XDCS.pin5
  N2: Esp32_GND->3_3V.pin3, ST7789_BL->GND.pin6
  N3: Esp32_GND->3_3V.pin6, ST7789_BL->GND.pin5
  N4: Esp32_GND->3_3V.pin7, VS1053_5V->XDCS.pin4
  N5: Esp32_GND->3_3V.pin8, VS1053_5V->XDCS.pin6
  N6: Esp32_GND->3_3V.pin9, VS1053_5V->XDCS.pin8
  N7: Esp32_GND->3_3V.pin10, VS1053_5V->XDCS.pin7
  N8: Esp32_GND->3_3V.pin11, VS1053_5V->XDCS.pin9
  N9: Esp32_GND->3_3V.pin12, ST7789_BL->GND.pin2
  N10: Esp32_GND->3_3V.pin13, ST7789_BL->GND.pin4
  N11: Esp32_GND->3_3V.pin14, VS1053_5V->XDCS.pin2, ESP32_3_3V->GND.pin17, IR.pin3, 74HC14.GND, C1.-, ST7789_BL->GND.pin8, Rele.pin2, C2.-, ON.pin2, VUp.pin2, C3.-, VDn.pin2, C4.-, C5.-, C6.-, ChUp.pin2, ChDn.pin2, Power_5V.pin1
  N12: Esp32_GND->3_3V.pin16, VS1053_5V->XDCS.pin1, VS1053_5V->XDCS.pin3, IR.pin2, 74HC14.VCC, C1.+, Rele.pin1, R1.Pin_1, R3.Pin_1, R5.Pin_1, R7.Pin_1, R8.Pin_1, Power_5V.pin2
  N13: Esp32_GND->3_3V.pin17, ST7789_BL->GND.pin7
  N14: ESP32_3_3V->GND.pin5, 74HC14.1Y
  N15: ESP32_3_3V->GND.pin6, 74HC14.4Y
  N16: ESP32_3_3V->GND.pin7, 74HC14.5Y
  N17: ESP32_3_3V->GND.pin8, 74HC14.6Y
  N18: ESP32_3_3V->GND.pin10, Rele.pin3
  N19: ESP32_3_3V->GND.pin11, ST7789_BL->GND.pin3
  N20: ESP32_3_3V->GND.pin12, ST7789_BL->GND.pin1
  N21: ESP32_3_3V->GND.pin13, 74HC14.2Y
  N22: ESP32_3_3V->GND.pin14, IR.pin1
  N23: 74HC14.1A, C5.+, R9.Pin_0
  N24: 74HC14.2A, C6.+, R10.Pin_0
  N25: 74HC14.4A, R2.Pin_0, C2.+
  N26: 74HC14.5A, R4.Pin_0, C3.+
  N27: 74HC14.6A, R6.Pin_0, C4.+
  N28: R1.Pin_0, R2.Pin_1, ON.pin1
  N29: R3.Pin_0, VUp.pin1, R4.Pin_1
  N30: R5.Pin_0, R6.Pin_1, VDn.pin1
  N31: R7.Pin_0, R9.Pin_1, ChUp.pin1
  N32: R8.Pin_0, R10.Pin_1, ChDn.pin1

notes:
  +
  -
  + 3.3V
  +3.3V
